// Logisim project GATE.circ as structural Verilog: 1 circuit, main circuit main
module main (
  input  A,
  input  A_2,
  input  B,
  input  B_2,
  input  C,
  input  C_2,
  input  A_3,
  input  B_3,
  input  C_3,
  output out_10
);

  wire transistor_1_out, transistor_2_out, transistor_3_out, transistor_7_out, transistor_8_out,
       transistor_9_out;

  Transistor #(.\type ("n")) transistor_1 (.in(1'b1), .out(transistor_1_out), .gate(A_2));
  Transistor #(.\type ("n")) transistor_2 (.in(transistor_1_out), .out(transistor_2_out), .gate(B_2));
  Transistor #(.\type ("n")) transistor_3 (.in(transistor_2_out), .out(transistor_3_out), .gate(C_2));
  Transistor transistor_4 (.in(1'b0), .out(transistor_3_out), .gate(A_2));
  Transistor transistor_5 (.in(1'b0), .out(transistor_3_out), .gate(B_2));
  Transistor transistor_6 (.in(1'b0), .out(transistor_3_out), .gate(C_2));
  // Probe on transistor_3_out
  Transistor transistor_7 (.in(1'b0), .out(transistor_7_out), .gate(A));
  Transistor transistor_8 (.in(transistor_7_out), .out(transistor_8_out), .gate(B));
  Transistor transistor_9 (.in(transistor_8_out), .out(transistor_9_out), .gate(C));
  Transistor #(.\type ("n")) transistor_10 (.in(1'b1), .out(transistor_9_out), .gate(A));
  Transistor #(.\type ("n")) transistor_11 (.in(1'b1), .out(transistor_9_out), .gate(B));
  Transistor #(.\type ("n")) transistor_12 (.in(1'b1), .out(transistor_9_out), .gate(C));
  // Probe on transistor_9_out

  assign out_10 = B_3;
  // also tied to GND on the sheet: B_3
endmodule
