// Logisim project mux.circ as structural Verilog: 1 circuit, main circuit main
module main (
  input  A,
  input  in_2,
  input  B,
  input  Ci1,
  output Si,
  output Ci
);

  wire and_1_out, and_3_out, and_4_out, and_5_out, and_6_out, and_7_out, and_8_out, not_1_out, not_2_out,
       not_3_out, not_4_out, not_5_out, not_6_out, not_7_out, not_8_out, not_9_out, not_10_out, not_11_out,
       not_12_out;

  not not_1 (not_1_out, A);
  not not_2 (not_2_out, B);
  not not_3 (not_3_out, Ci1);
  not not_4 (not_4_out, A);
  not not_5 (not_5_out, B);
  not not_6 (not_6_out, A);
  not not_7 (not_7_out, Ci1);
  not not_8 (not_8_out, A);
  not not_9 (not_9_out, B);
  not not_10 (not_10_out, Ci1);
  not not_11 (not_11_out, B);
  not not_12 (not_12_out, Ci1);
  and and_1 (and_1_out, A, B, Ci1);
  // AND_Gate and_2 has open pins: in0=not_1_out, in1=not_2_out, in2=not_3_out, out=open
  and and_3 (and_3_out, not_4_out, not_5_out, Ci1);
  and and_4 (and_4_out, not_6_out, B, not_7_out);
  and and_5 (and_5_out, not_8_out, B, Ci1);
  and and_6 (and_6_out, A, not_9_out, not_10_out);
  and and_7 (and_7_out, A, not_11_out, Ci1);
  and and_8 (and_8_out, A, B, not_12_out);
  or or_1 (Si, in_2, and_3_out, and_4_out, and_7_out, in_2, and_1_out);
  or or_2 (Ci, and_5_out, and_7_out, and_8_out, and_1_out, in_2, in_2);
endmodule
