// Logisim project sel.circ as structural Verilog: 1 circuit, main circuit main
module main (
  input  A,
  input  B,
  input  CONSTANT,
  input  CONSTANT_2,
  input  CONSTANT_3,
  input  CONSTANT_4,
  output OUTPUT
);

  wire and_1_out, and_2_out, and_3_out, and_4_out, and_5_out, and_6_out, not_1_out, not_2_out, not_3_out,
       or_1_out, or_2_out;

  not not_1 (not_1_out, A);
  and and_1 (and_1_out, not_1_out, CONSTANT);
  and and_2 (and_2_out, A, CONSTANT_2);
  or or_1 (or_1_out, and_1_out, and_2_out);
  not not_2 (not_2_out, A);
  and and_3 (and_3_out, not_2_out, CONSTANT_3);
  and and_4 (and_4_out, A, CONSTANT_4);
  or or_2 (or_2_out, and_3_out, and_4_out);
  not not_3 (not_3_out, B);
  and and_5 (and_5_out, not_3_out, or_1_out);
  and and_6 (and_6_out, B, or_2_out);
  or or_3 (OUTPUT, and_5_out, and_6_out);
endmodule
