// Logisim project test.circ as structural Verilog: 1 circuit, main circuit main
module main (
  input  in_1
);

  wire CLK_INSTR_out;
  wire [7:0] PC_HIGH_q;
  wire [31:0] ram_1_data, undriven, undriven_2;

  Clock CLK_INSTR (.out(CLK_INSTR_out));
  Register PC_HIGH (.Q(PC_HIGH_q), .clk(CLK_INSTR_out));  // open: D, en, clr
  Register #(.width(24)) PC_LOW (.Q({PC_HIGH_q, PC_HIGH_q, PC_HIGH_q}), .clk(CLK_INSTR_out));  // open: D, en, clr
  RAM #(.dataWidth(32)) ram_1 (.addr(PC_HIGH_q), .data(ram_1_data));  // open: sel, clk, ld, clr
  Register #(.width(32)) data_if_id (.D(ram_1_data));  // open: en, Q, clk, clr
  Register #(.width(32)) register_1 ();  // open: D, en, Q, clk, clr
  Register #(.width(32)) pc_if_id (.D({PC_HIGH_q, PC_HIGH_q, PC_HIGH_q, PC_HIGH_q}));  // open: en, Q, clk, clr
  Register #(.width(32)) register_2 ();  // open: D, en, Q, clk, clr
  Decoder decoder_1 ();  // open: out0, out1, sel, en
  Register #(.width(32)) data_if_id_2 ();  // open: D, en, Q, clk, clr
  Register #(.width(32)) register_3 ();  // open: D, en, Q, clk, clr
  Register #(.width(32)) pc_if_id_2 (.D(undriven));  // open: en, Q, clk, clr
  Register #(.width(32)) register_4 ();  // open: D, en, Q, clk, clr
  Register #(.width(32)) data_if_id_3 ();  // open: D, en, Q, clk, clr
  Register #(.width(32)) register_5 ();  // open: D, en, Q, clk, clr
  Register #(.width(32)) pc_if_id_3 (.D(undriven_2));  // open: en, Q, clk, clr
  Register #(.width(32)) register_6 ();  // open: D, en, Q, clk, clr

  // Notes on the sheet:
  //   IF
  //   ID
  //   EX
  //   MEM_STORE
endmodule
